# Fritzing sketch roboFeeder (saved by Fritzing 0.9.1b)
breadboards: 1

parts:
  Raspberry_Pi_A1 = Raspberry Pi A
  IC1 = L293D [package=THT]
  Part1 = Logic Level Converter
  Shutdown_Switch = Pushbutton [package="[THT]"]
  PIR_Sensor = Infrared Proximity Sensor
  RFID1 = RFID Reader
  Power_plug1 = Power plug
  R1 = Resistor [tolerance=±5% resistance=220 package="0603 [SMD]"]
  BAT1 = Battery Holders [package=battery-aa-panel]
  Reset_Switch = Round Pushbutton  # not connected
  ANT1 = Antenna
  R2 = Resistor [tolerance=±5% resistance=1k package=THT]
  R3 = Resistor [tolerance=±5% resistance=10k package="0603 [SMD]"]
  V1 = DC Power [voltage=5]
  Drive_Motor = DC Motor

nets:
  N1: Raspberry_Pi_A1.3V3, Part1.LV
  5V: Raspberry_Pi_A1.5V, Part1.HV, Power_plug1.VCC
  GND: Raspberry_Pi_A1.GND, IC1.0V, Part1.GND, PIR_Sensor.GND, RFID1.GND, Power_plug1.GND, BAT1.+, R3.Pin_1, V1.V-
  N2: Raspberry_Pi_A1.GPIO_23, IC1.In_2
  N3: Raspberry_Pi_A1.GPIO_15, Part1.TX_LV
  N4: Raspberry_Pi_A1.GPIO_17, PIR_Sensor.Vcc
  N5: Raspberry_Pi_A1.GPIO_18, R1.Pin_0
  N6: Raspberry_Pi_A1.GPIO_4, R2.Pin_1
  N7: Raspberry_Pi_A1.GPIO_24, IC1.In_1
  N8: Raspberry_Pi_A1.GPIO_25, IC1.Enable_1
  N9: IC1.Out_1_(_Controlled_by_Enable_1_), Drive_Motor.pin_1
  N10: IC1.Out_2_(_Controlled_by_Enable_1_), Drive_Motor.pin_2
  N11: IC1.+Vmotor, BAT1.-
  N12: Part1.RX_HV, RFID1.Future
  N13: Shutdown_Switch.Pin_1, Shutdown_Switch.Pin_2, R2.Pin_0, R3.Pin_0
  N14: Shutdown_Switch.Pin_3, RFID1.+5V, V1.V+
  N15: PIR_Sensor.Vout, R1.Pin_1
  N16: RFID1.ANT0, RFID1.ANT1, ANT1.antenna_lead
